# Fritzing sketch scheme (saved by Fritzing 0.9.3b)

parts:
  U1 = ESP8266 WiFi Module [part_number=ESP8266]
  KY-1 = Keyes Relay [package=THT]

nets:
  N1: U1.GPIO_2, KY-1.signal

notes:
  3.3v
  5v
  Lamp

custom parts:
  ESP8266 WiFi Module: Generic WiFi Module based on the ESP8266 with onboard PCB antenna and UART communications
  Keyes Relay: The Keyes 5V relay module is suitable for SCM development, home appliance control. It uses a 5V~12V TIL control signal which can control DC / AC signal.
