# Fritzing sketch scheme_1 (saved by Fritzing 0.9.3b)

parts:
  U1 = ESP8266 WiFi Module [part_number=ESP8266]
  Q1 = NPN-Transistor [package="SOT-23 [SMD]"]
  R1 = Resistor [tolerance=±10% resistance=1k package="2010 [SMD]"]
  R2 = Resistor [tolerance=±5% resistance=10k package="2010 [SMD]"]

nets:
  N1: U1.VCC, U1.CH_PD
  N2: U1.GPIO_2, R1.Pin_0
  N3: Q1.0, R2.Pin_0

notes:
  Lamp
  3.3V
  +
  -

custom parts:
  ESP8266 WiFi Module: Generic WiFi Module based on the ESP8266 with onboard PCB antenna and UART communications
