# Fritzing sketch scheme (saved by Fritzing 0.9.3b)

parts:
  U1 = ESP8266 WiFi Module [part_number=ESP8266]
  T1 = LM35 Temperature Sensor [package="TO92 [THT]"]

nets:
  N1: U1.GPIO_2, T1.Vout

notes:
  3.3v
  5v

custom parts:
  ESP8266 WiFi Module: Generic WiFi Module based on the ESP8266 with onboard PCB antenna and UART communications
